// Logisim project circuit_design.circ as structural Verilog: 1 circuit, main circuit main
module main (
  input  in_1,
  input  in_2,
  input  in_3,
  input  in_4,
  input  in_5,
  input  in_6,
  input  in_7,
  input  in_8,
  input  in_9,
  input  in_10,
  input  in_11,
  output out_12
);

  Multiplexer #(.select(3), .enable("false")) multiplexer_1 (
    .in0(in_1), .in1(in_2), .in2(in_3), .in3(in_4), .in4(in_5), .in5(in_7), .in6(in_9), .in7(in_11),
    .out(out_12), .sel({in_10, in_8, in_6}));
endmodule
